// Logisim project project_v2.circ as structural Verilog: 2 circuits, main circuit main
module main (
  input  in_1,
  input  A,
  input  in_3,
  input  in_4,
  input  in_5,
  input  in_6,
  input  in_7,
  input  in_8,
  input  in_9,
  input  in_10,
  input  in_11
);

  wire a1_t, a_t_t, Aa, Ab, Ac, Ad, adder_1_cout, adder_2_cout, adder_3_cout, Ae, Af, Ag, b1_t, b_t, Ba, Bb,
       Bc, Bd, Be, Bf, Bg, c, c1, Cout, d, d1, e, e1, f, f1, g, g1, S1, S2, S3, S4, xor_1_out, xor_2_out,
       xor_3_out, xor_4_out;
  wire [3:0] AND, multiplexer_1_out, OR, XOR;

  _7_segment u_7_segment_1 (
    .in_1(in_4), .in_2(in_3), .in_3(A), .in_4(in_1), .out_5(Aa), .out_6(Ab), .out_7(Ac), .out_8(Ad),
    .out_9(Ae), .out_10(Af), .out_11(Ag));
  _7_segment u_7_segment_2 (
    .in_1(in_11), .in_2(in_10), .in_3(in_9), .in_4(in_8), .out_5(Ba), .out_6(Bb), .out_7(Bc), .out_8(Bd),
    .out_9(Be), .out_10(Bf), .out_11(Bg));
  _7_Segment_Display u_7_segment_display_1 (.g(Ag), .f(Af), .a(Aa), .b(Ab), .e(Ae), .d(Ad), .c(Ac));  // open: dp
  _7_Segment_Display u_7_segment_display_2 (.g(Bg), .f(Bf), .a(Ba), .b(Bb), .e(Be), .d(Bd), .c(Bc));  // open: dp
  xor xor_1 (xor_1_out, in_5, in_11);
  xor xor_2 (xor_2_out, in_5, in_10);
  xor xor_3 (xor_3_out, in_5, in_9);
  xor xor_4 (xor_4_out, in_5, in_8);
  assign AND = {in_1, A, in_3, in_4} & {in_8, in_9, in_10, in_11};  // AND_Gate and_1, 4 bits wide
  assign OR = {in_1, A, in_3, in_4} | {in_8, in_9, in_10, in_11};  // OR_Gate or_1, 4 bits wide
  Adder #(.width(1)) adder_1 (.a(in_4), .b(xor_1_out), .out(S1), .cin(in_5), .cout(adder_1_cout));
  Adder #(.width(1)) adder_2 (.a(in_3), .b(xor_2_out), .out(S2), .cin(adder_1_cout), .cout(adder_2_cout));
  Adder #(.width(1)) adder_3 (.a(A), .b(xor_3_out), .out(S3), .cin(adder_2_cout), .cout(adder_3_cout));
  Adder #(.width(1)) adder_4 (.a(in_1), .b(xor_4_out), .out(S4), .cin(adder_3_cout), .cout(Cout));
  assign XOR = {in_1, A, in_3, in_4} ^ {in_8, in_9, in_10, in_11};  // XOR_Gate xor_5, 4 bits wide
  Multiplexer #(.select(2), .width(4)) multiplexer_1 (
    .in0({S4, S3, S2, S1}), .in1(AND), .in2(OR), .in3(XOR), .out(multiplexer_1_out), .sel({in_6, in_7}));  // open: en
  _7_segment u_7_segment_3 (
    .in_1(multiplexer_1_out[0]), .in_2(multiplexer_1_out[1]), .in_3(multiplexer_1_out[2]),
    .in_4(multiplexer_1_out[3]), .out_5(a_t_t), .out_6(b_t), .out_7(c), .out_8(d), .out_9(e), .out_10(f),
    .out_11(g));
  _7_segment u_7_segment_4 (
    .in_1(Cout), .in_2(1'b0), .in_3(1'b0), .in_4(1'b0), .out_5(a1_t), .out_6(b1_t), .out_7(c1), .out_8(d1),
    .out_9(e1), .out_10(f1), .out_11(g1));
  _7_Segment_Display u_7_segment_display_3 (.g(g1), .f(f1), .a(a1_t), .b(b1_t), .e(e1), .d(d1), .c(c1));  // open: dp
  _7_Segment_Display u_7_segment_display_4 (.g(g), .f(f), .a(a_t_t), .b(b_t), .e(e), .d(d), .c(c));  // open: dp

  // Other names for the same wires on the sheet: A1 = in_4; A_t[3:0] = {in_1, A, in_3, in_4}; A2 = in_3; A3 = A;
  //   A4 = in_1; B[3:0] = {in_8, in_9, in_10, in_11}; B1 = in_11; B2 = in_10; B3 = in_9; B4 = in_8; m = in_5

  // Notes on the sheet:
  //   inputs
  //   B
  //   calculation
  //   output
endmodule

module _7_segment (
  input  in_1,
  input  in_2,
  input  in_3,
  input  in_4,
  output out_5,
  output out_6,
  output out_7,
  output out_8,
  output out_9,
  output out_10,
  output out_11
);

  wire _0, _1, _2, _3, _4, _5, _6, _7, _8, _9, _10, _11, _12, _13, _14, _15;

  Decoder #(.select(4)) decoder_1 (
    .out0(_0), .out1(_1), .out2(_2), .out3(_3), .out4(_4), .out5(_5), .out6(_6), .out7(_7), .out8(_8),
    .out9(_9), .out10(_10), .out11(_11), .out12(_12), .out13(_13), .out14(_14), .out15(_15),
    .sel({in_4, in_3, in_2, in_1}));  // open: en
  or or_1 (out_5, _0, _2, _3, _5, _6, _7, _8, _9, _10, _12, _14, _15);
  _7_Segment_Display u_7_segment_display_1 (
    .g(out_11), .f(out_10), .a(out_5), .b(out_6), .e(out_9), .d(out_8), .c(out_7));  // open: dp
  or or_2 (out_6, _0, _1, _2, _3, _4, _7, _8, _9, _10, _13);
  or or_3 (out_7, _0, _1, _3, _4, _5, _6, _7, _8, _9, _10, _11, _13);
  or or_4 (out_8, _0, _2, _3, _5, _6, _8, _11, _12, _13, _14);
  or or_5 (out_9, _0, _2, _6, _8, _10, _11, _12, _13, _14, _15);
  or or_6 (out_10, _0, _4, _5, _6, _8, _9, _10, _11, _12, _14, _15);
  or or_7 (out_11, _2, _3, _4, _5, _6, _8, _9, _10, _11, _13, _14, _15);

  // Other names for the same wires on the sheet: a = out_5; b = out_6; c = out_7; d = out_8; e = out_9; f = out_10;
  //   g = out_11; in[3:0] = {in_4, in_3, in_2, in_1}

  // Notes on the sheet:
  //   7 segment display
endmodule
